// Logisim project cpu.circ as structural Verilog: 8 circuits, main circuit main
module main (
);

  wire clock_1_out, dipswitch_2_p4, reset_out;
  wire [2:0] CPU_address_bus, dipswitch_2_p1;
  wire [7:0] output_q;
  wire [8:0] CPU_output_bus;
  wire [14:0] dipswitch_1_p1, RAM_data_out;

  Clock clock_1 (.out(clock_1_out));
  cpu CPU (
    .clock(clock_1_out), .address_bus(CPU_address_bus), .data_in_bus(RAM_data_out), .reset(reset_out),
    .output_bus(CPU_output_bus));
  ram RAM (.addr(CPU_address_bus), .data_out(RAM_data_out));  // open: write, data_in
  Register #(.trigger("falling")) \output  (
    .D(CPU_output_bus[7:0]), .Q(output_q), .clk(CPU_output_bus[8]), .clr(reset_out));  // open: en
  Button reset (.out(reset_out));
  // Probe on output_q
  // DipSwitch #(.NSwitches(15)) dipswitch_1: pin names not known; wires that end beside it: dipswitch_1_p1[0], dipswitch_1_p1[1], dipswitch_1_p1[2], dipswitch_1_p1[3], dipswitch_1_p1[4], dipswitch_1_p1[5], dipswitch_1_p1[6], dipswitch_1_p1[7], dipswitch_1_p1[8], dipswitch_1_p1[9], dipswitch_1_p1[10], dipswitch_1_p1[11], dipswitch_1_p1[12], dipswitch_1_p1[13], dipswitch_1_p1[14], dipswitch_1_p1
  // DipSwitch #(.NSwitches(3)) dipswitch_2: pin names not known; wires that end beside it: dipswitch_2_p1[0], dipswitch_2_p1[1], dipswitch_2_p1[2], dipswitch_2_p4, dipswitch_2_p1
  Button button_1 (.out(dipswitch_2_p4));
endmodule

module ALU (
  input  clock,
  input  op,
  input  [7:0] X,
  input  [7:0] Y,
  output [7:0] Output,
  output CF,
  output ZF
);

  wire [7:0] and_1_out, and_2_out, xor_1_out;

  assign and_1_out = {8{clock}} & X;  // AND_Gate and_1, 8 bits wide
  assign and_2_out = {8{clock}} & Y;  // AND_Gate and_2, 8 bits wide
  assign xor_1_out = {8{op}} ^ and_2_out;  // XOR_Gate xor_1, 8 bits wide
  Adder adder_1 (.a(and_1_out), .b(xor_1_out), .out(Output), .cin(op), .cout(CF));
  nor nor_1 (ZF, Output[7], Output[6], Output[5], Output[4], Output[3], Output[2], Output[1], Output[0]);
endmodule

module register_file (
  input  [2:0] s_out1,
  input  [2:0] s_out2,
  input  [2:0] s_in,
  input  clock,
  input  [7:0] data_in,
  input  reset,
  output [7:0] data_out1,
  output [7:0] data_out2
);

  wire demultiplexer_1_out0, demultiplexer_1_out1, demultiplexer_1_out2, demultiplexer_1_out3,
       demultiplexer_1_out4, demultiplexer_1_out5, demultiplexer_1_out6, demultiplexer_1_out7;
  wire [7:0] _0_q, _1_q, _2_q, _3_q, _4_q, _5_q, _6_q, _7_q;

  Demultiplexer #(.select(3), .enable("false")) demultiplexer_1 (
    .out0(demultiplexer_1_out0), .out1(demultiplexer_1_out1), .out2(demultiplexer_1_out2),
    .out3(demultiplexer_1_out3), .out4(demultiplexer_1_out4), .out5(demultiplexer_1_out5),
    .out6(demultiplexer_1_out6), .out7(demultiplexer_1_out7), .in(clock), .sel(s_in));
  Register _0 (.D(data_in), .Q(_0_q), .clk(demultiplexer_1_out0), .clr(reset));  // open: en
  Register _2 (.D(data_in), .Q(_2_q), .clk(demultiplexer_1_out2), .clr(reset));  // open: en
  Register _4 (.D(data_in), .Q(_4_q), .clk(demultiplexer_1_out4), .clr(reset));  // open: en
  Register _6 (.D(data_in), .Q(_6_q), .clk(demultiplexer_1_out6), .clr(reset));  // open: en
  Register _1 (.D(data_in), .Q(_1_q), .clk(demultiplexer_1_out1), .clr(reset));  // open: en
  Register _3 (.D(data_in), .Q(_3_q), .clk(demultiplexer_1_out3), .clr(reset));  // open: en
  Register _5 (.D(data_in), .Q(_5_q), .clk(demultiplexer_1_out5), .clr(reset));  // open: en
  Register _7 (.D(data_in), .Q(_7_q), .clk(demultiplexer_1_out7), .clr(reset));  // open: en
  Multiplexer #(.select(3), .width(8), .enable("false")) multiplexer_1 (
    .in0(_0_q), .in1(_1_q), .in2(_2_q), .in3(_3_q), .in4(_4_q), .in5(_5_q), .in6(_6_q), .in7(_7_q),
    .out(data_out1), .sel(s_out1));
  Multiplexer #(.select(3), .width(8), .enable("false")) multiplexer_2 (
    .in0(_0_q), .in1(_1_q), .in2(_2_q), .in3(_3_q), .in4(_4_q), .in5(_5_q), .in6(_6_q), .in7(_7_q),
    .out(data_out2), .sel(s_out2));
endmodule

module ram (
  input  [2:0] addr,
  input  write,
  input  [14:0] data_in,
  output [14:0] data_out
);

  wire demultiplexer_1_out0, demultiplexer_1_out1, demultiplexer_1_out2, demultiplexer_1_out3,
       demultiplexer_1_out4, demultiplexer_1_out5, demultiplexer_1_out6, demultiplexer_1_out7;
  wire [14:0] _0_q, _1_q, _2_q, _3_q, _4_q, _5_q, _6_q, _7_q;

  Demultiplexer #(.select(3), .enable("false")) demultiplexer_1 (
    .out0(demultiplexer_1_out0), .out1(demultiplexer_1_out1), .out2(demultiplexer_1_out2),
    .out3(demultiplexer_1_out3), .out4(demultiplexer_1_out4), .out5(demultiplexer_1_out5),
    .out6(demultiplexer_1_out6), .out7(demultiplexer_1_out7), .in(write), .sel(addr));
  Register #(.width(15)) _0 (.D(data_in), .Q(_0_q), .clk(demultiplexer_1_out0));  // open: en, clr
  Register #(.width(15)) _2 (.D(data_in), .Q(_2_q), .clk(demultiplexer_1_out2));  // open: en, clr
  Register #(.width(15)) _4 (.D(data_in), .Q(_4_q), .clk(demultiplexer_1_out4));  // open: en, clr
  Register #(.width(15)) _6 (.D(data_in), .Q(_6_q), .clk(demultiplexer_1_out6));  // open: en, clr
  Register #(.width(15)) _1 (.D(data_in), .Q(_1_q), .clk(demultiplexer_1_out1));  // open: en, clr
  Register #(.width(15)) _3 (.D(data_in), .Q(_3_q), .clk(demultiplexer_1_out3));  // open: en, clr
  Register #(.width(15)) _5 (.D(data_in), .Q(_5_q), .clk(demultiplexer_1_out5));  // open: en, clr
  Register #(.width(15)) _7 (.D(data_in), .Q(_7_q), .clk(demultiplexer_1_out7));  // open: en, clr
  Multiplexer #(.select(3), .width(15), .enable("false")) multiplexer_1 (
    .in0(_0_q), .in1(_1_q), .in2(_2_q), .in3(_3_q), .in4(_4_q), .in5(_5_q), .in6(_6_q), .in7(_7_q),
    .out(data_out), .sel(addr));
endmodule

module clock (
  input  in_1,
  output fetch,
  output decode,
  output execute,
  output write
);

  wire [1:0] adder_1_out, register_1_q;

  Register #(.width(2)) register_1 (.D(adder_1_out), .Q(register_1_q), .clk(in_1));  // open: en, clr
  Adder #(.width(2)) adder_1 (.a(register_1_q), .b(2'b01), .out(adder_1_out));  // open: cin, cout
  // Probe on register_1_q
  Demultiplexer #(.select(2), .enable("false")) demultiplexer_1 (
    .out0(fetch), .out1(decode), .out2(execute), .out3(write), .in(1'b1), .sel(register_1_q));
endmodule

module pc (
  input  clock,
  input  [2:0] jmpadd,
  input  write,
  input  reset,
  output [2:0] inst
);

  wire [2:0] adder_1_out, multiplexer_1_out;

  Register #(.width(3)) register_1 (.D(multiplexer_1_out), .Q(inst), .clk(clock), .clr(reset));  // open: en
  Adder #(.width(3)) adder_1 (.a(inst), .b(3'b000), .out(adder_1_out), .cin(1'b1));  // open: cout
  Multiplexer #(.width(3), .enable("false")) multiplexer_1 (
    .in0(adder_1_out), .in1(jmpadd), .out(multiplexer_1_out), .sel(write));
endmodule

module cpu (
  input  clock,
  input  [14:0] data_in_bus,
  input  reset,
  output [8:0] output_bus,
  output [2:0] address_bus
);

  wire and_1_out, and_2_out, and_3_out, clock_decode, clock_execute, clock_fetch, clock_write, d_ff_1_q,
       decoder_1_out1, decoder_1_out2, decoder_1_out3, decoder_1_out7, dipswitch_2_p4, not_1_out, not_2_out,
       not_3_out, or_1_out;
  wire [1:0] ALU_zf, flags_q;
  wire [2:0] dipswitch_2_p1, multiplexer_2_out;
  wire [7:0] ALU_output, multiplexer_3_out, Regs_data_out1, Regs_data_out2;
  wire [7:3] multiplexer_2_out_2;
  wire [14:0] dipswitch_1_p1, IR_q, multiplexer_1_out;

  and and_1 (and_1_out, clock, not_1_out);
  not not_1 (not_1_out, d_ff_1_q);
  clock u_clock (
    .in_1(and_1_out), .fetch(clock_fetch), .decode(clock_decode), .execute(clock_execute), .write(clock_write));
  pc PC (.clock(clock_fetch), .reset(reset), .inst(address_bus), .jmpadd(multiplexer_2_out), .write(decoder_1_out3));
  Multiplexer #(.width(15), .enable("false")) multiplexer_1 (
    .in0(data_in_bus), .in1({15{1'b0}}), .out(multiplexer_1_out), .sel(and_2_out));
  and and_2 (and_2_out, flags_q[0], IR_q[13]);
  // Probe on ALU_output
  ALU ALU (
    .clock(clock_execute), .op(decoder_1_out1), .X(multiplexer_3_out),
    .Y({multiplexer_2_out_2, multiplexer_2_out}), .CF(ALU_zf[1]), .ZF(ALU_zf[0]), .Output(ALU_output));
  Register #(.width(15)) IR (.D(multiplexer_1_out), .Q(IR_q), .clk(clock_decode));  // open: en, clr
  not not_2 (not_2_out, or_1_out);
  and and_3 (and_3_out, clock_write, not_2_out);
  Register #(.width(2)) flags (.D(ALU_zf), .Q(flags_q), .clk(and_3_out), .clr(reset));  // open: en
  register_file Regs (
    .clock(and_3_out), .data_in(ALU_output), .s_in(IR_q[14:12]), .s_out1({IR_q[9], IR_q[10], IR_q[11]}),
    .s_out2(IR_q[14:12]), .reset(reset), .data_out1(Regs_data_out1), .data_out2(Regs_data_out2));
  Multiplexer #(.width(8), .enable("false")) multiplexer_2 (
    .in0(Regs_data_out1), .in1({IR_q[4], IR_q[5], IR_q[6], IR_q[7], IR_q[8], IR_q[9], IR_q[10], IR_q[11]}),
    .out({multiplexer_2_out_2, multiplexer_2_out}), .sel(not_3_out));
  not not_3 (not_3_out, IR_q[3]);
  Decoder #(.select(3), .enable("false")) decoder_1 (
    .out1(decoder_1_out1), .out2(decoder_1_out2), .out3(decoder_1_out3), .out4(output_bus[8]),
    .out7(decoder_1_out7), .sel(IR_q[2:0]));  // open: out0, out5, out6
  // Probe on Regs_data_out2
  Multiplexer #(.width(8), .enable("false")) multiplexer_3 (
    .in0(Regs_data_out2), .in1({8{1'b0}}), .out(multiplexer_3_out), .sel(decoder_1_out2));
  Multiplexer #(.width(8), .enable("false")) multiplexer_4 (
    .in0({8{1'b0}}), .in1(Regs_data_out2), .out(output_bus[7:0]), .sel(output_bus[8]));
  or or_1 (or_1_out, decoder_1_out3, output_bus[8]);
  D_Flip_Flop d_ff_1 (.clk(clock_execute), .D(decoder_1_out7), .Q(d_ff_1_q), .reset(reset));  // open: Qn, preset
  // DipSwitch #(.NSwitches(15)) dipswitch_1: pin names not known; wires that end beside it: dipswitch_1_p1[0], dipswitch_1_p1[1], dipswitch_1_p1[2], dipswitch_1_p1[3], dipswitch_1_p1[4], dipswitch_1_p1[5], dipswitch_1_p1[6], dipswitch_1_p1[7], dipswitch_1_p1[8], dipswitch_1_p1[9], dipswitch_1_p1[10], dipswitch_1_p1[11], dipswitch_1_p1[12], dipswitch_1_p1[13], dipswitch_1_p1[14], dipswitch_1_p1
  // DipSwitch #(.NSwitches(3)) dipswitch_2: pin names not known; wires that end beside it: dipswitch_2_p1[0], dipswitch_2_p1[1], dipswitch_2_p1[2], dipswitch_2_p4, dipswitch_2_p1
  Button button_1 (.out(dipswitch_2_p4));
endmodule

module computer (
);

  wire clock_1_out, dipswitch_2_p4, reset_out;
  wire [2:0] CPU_address_bus, dipswitch_2_p1;
  wire [7:0] output_q;
  wire [8:0] CPU_output_bus;
  wire [14:0] dipswitch_1_p1, RAM_data_out;

  Clock clock_1 (.out(clock_1_out));
  // Probe on CPU_address_bus
  cpu CPU (
    .clock(clock_1_out), .address_bus(CPU_address_bus), .data_in_bus(RAM_data_out), .reset(reset_out),
    .output_bus(CPU_output_bus));
  ram RAM (.addr(CPU_address_bus), .data_out(RAM_data_out));  // open: write, data_in
  Register #(.trigger("falling")) \output  (
    .D(CPU_output_bus[7:0]), .Q(output_q), .clk(CPU_output_bus[8]), .clr(reset_out));  // open: en
  Button reset (.out(reset_out));
  // Probe on output_q
  // DipSwitch #(.NSwitches(15)) dipswitch_1: pin names not known; wires that end beside it: dipswitch_1_p1[0], dipswitch_1_p1[1], dipswitch_1_p1[2], dipswitch_1_p1[3], dipswitch_1_p1[4], dipswitch_1_p1[5], dipswitch_1_p1[6], dipswitch_1_p1[7], dipswitch_1_p1[8], dipswitch_1_p1[9], dipswitch_1_p1[10], dipswitch_1_p1[11], dipswitch_1_p1[12], dipswitch_1_p1[13], dipswitch_1_p1[14], dipswitch_1_p1
  // DipSwitch #(.NSwitches(3)) dipswitch_2: pin names not known; wires that end beside it: dipswitch_2_p1[0], dipswitch_2_p1[1], dipswitch_2_p1[2], dipswitch_2_p4, dipswitch_2_p1
  Button button_1 (.out(dipswitch_2_p4));
endmodule
